# Fritzing sketch Temp_monitor_device_fritzing (saved by Fritzing 1.0.4)
breadboards: 1

parts:
  A1 = Particle - Photon2
  S1 = Round Pushbutton
  M1 = BMP280
  R1 = Resistor [tolerance=±5% resistance=220 package="2010 [SMD]"]
  S2 = Toggle Switch [package=THT]
  LED2 = LED - 5mm [color="Green (555nm)" current=0.030A package="5 mm [THT]"]
  A2 = nozzle-bolt style thermocouple [package=THT]
  A3 = MAX6675 module [package=THT]
  OLED_I2C1 = OLED 128x64 I2C Monochrome Display

nets:
  N1: A1.Pin_17, M1.SDA, OLED_I2C1.SDA
  N2: A1.Pin_18, M1.SCL, OLED_I2C1.SCK
  N3: A1.Pin_20, A3.pin5
  N4: A1.Pin_21, A3.pin3
  N5: A1.Pin_22, A3.pin4
  N6: A1.Pin_23, S1.leg0
  N7: A1.Pin_24, A1.Pin_36, R1.Pin_0, R1.Pin_1, LED2.anode
  N8: A1.Pin_27, S2.L1
  GND: S1.leg1, M1.GND, S2.COM, LED2.cathode, A3.pin1, OLED_I2C1.GND
  VIN: M1.VIN, A3.pin2, OLED_I2C1.VDD
  N9: A2.pin1, A3.pin7
  N10: A2.pin2, A3.pin6

notes:
  PINS:
  D7 - Power indicator LED
  D6 - Start Monitoring (Cancel Monitoring)
  D5 - Thermocouple CS
  D3 - Thermocouple MISO
  D4 - Thermocouple SCK
  D1 -OLED SCK & BME SCK
  D0 - OLED SDA & BME
  EN - Power switch
  TEMP SENSOR
  COMPONENTS:
  Photon 2 - microcontroller
  Thermocouple probe
  MAX6675 - to read Temp with probe
  OLED - Display
  BME280 - to calculate elevation for boiling point
  SPST Switch - start/cancel
  DPST Switch - power
  Green LED
  220Ohm resistor
  Temp Monitor
  Schematic

custom parts:
  Particle - Photon2: The Photon 2 is a microcontroller and Wi-Fi networking developed by particle. Features: 802.11a/b/g/n Wi-Fi, 2.4 GHz and 5 GHz Integrated PCB antenna Integrated U.FL connector for external antenna Integrated RF switch BLE 5 using same antenna as Wi-Fi Realtek RTL8721DM MCU ARM Cortex M33 CPU, 200 MHz 2048 KB (2 MB) user application maximum size 3072 KB (3 MB) of RAM available to user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
  BMP280: Temperature Humidity Barometric presure Sensor, I2C
  nozzle-bolt style thermocouple: Generic nozzle-bolt style thermocouple.
  MAX6675 module: MAX6675 Module + K Type Thermocouple Sensor Temperature Degrees.
